# Fritzing sketch turret (saved by Fritzing 0.8.7b)
breadboards: 1

parts:
  Arduino_Uno = Arduino Uno (Rev3)
  IC1 = L293D [package=THT]
  M1 = DC Motor

nets:
  N1: Arduino_Uno.D11_PWM/MOSI, IC1.In_1
  N2: Arduino_Uno.D12/MISO, IC1.In_2
  N3: Arduino_Uno.D13/SCK, IC1.Enable_1
  N4: Arduino_Uno.5V, IC1.+V
  GND: Arduino_Uno.GND, Arduino_Uno.VIN, IC1.0V, IC1.+Vmotor
  N5: IC1.Out_1_(_Controlled_by_Enable_1_), M1.pin_1
  N6: IC1.Out_2_(_Controlled_by_Enable_1_), M1.pin_2
